# Fritzing sketch schematic (saved by Fritzing 0.9.4)
breadboards: 1

parts:
  DFRobot_DFPlayer_Mini1 = DFRobot DFPlayer Mini [part_number=DFR0299]
  HC-SR04_Sensor_1 = HC-SR04 Ultrasonic Distance Sensor
  Part2 = 12 NeoPixel Ring [part_number=1643]
  R1 = Resistor [tolerance=±5% resistance=1k package=THT]
  V1 = DC Power [voltage=5]
  Part3 = ESP-WROOM-32 [ESP-32S] Module [part_number=ESP-WROOM-32]
  SP1 = SPEAKER [package=pcb_mount_speaker]

nets:
  VCC: DFRobot_DFPlayer_Mini1.VCC, HC-SR04_Sensor_1.VCC, Part2.VDD, V1.V+
  N1: DFRobot_DFPlayer_Mini1.RX, R1.Pin_1
  N2: DFRobot_DFPlayer_Mini1.TX, Part3.IO17
  N3: DFRobot_DFPlayer_Mini1.SPK_1, SP1.-
  N4: DFRobot_DFPlayer_Mini1.GND-1, DFRobot_DFPlayer_Mini1.GND-2, HC-SR04_Sensor_1.ECHO, Part2.GND, V1.V-
  N5: DFRobot_DFPlayer_Mini1.SPK_2, SP1.+
  N6: HC-SR04_Sensor_1.TRIG, Part3.IO15
  N7: HC-SR04_Sensor_1.GND, Part3.IO4
  N8: Part2.IN, Part3.IO32
  N9: R1.Pin_0, Part3.IO16

custom parts:
  12 NeoPixel Ring: 12 ultra bright smart LED NeoPixels are arranged in a circle with 1.5" (37mm) outer diameter. The rings are 'chainable' - connect the output pin of one to the input pin of another. Use only one microcontroller pin to control as many as you can chain together! Each LED is addressable as the driver chip is inside the LED. Each one has ~18mA constant current drive so the color will be very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
  ESP-WROOM-32 [ESP-32S] Module: Espressif ESP-WROOM-32 WiFi/Bluetooth LE microcontroller module also known as the Ai-Thinker ESP-32S module with similar formfactor. The ESP32 is a microcontroller chip with WiFi and BLE capabilities. The chip is developed by Espressif and is the successor to the popular ESP8266 WiFi module.
